# Fritzing sketch RCPulseInJoystickServoControl (saved by Fritzing 0.9.2b)
breadboards: 1

parts:
  IC1 = L293D [package=THT]
  Uno = Arduino Uno (Rev3) - ICSP
  M1 = DC Motor
  M2 = DC Motor
  VCC2 = 4 x AAA Battery Mount
  VCC3 = Battery block 9V
  5V_power_switch = SWITCH_SPDT [package=kps-1290]
  Battery_Switch = SWITCH_SPDT [package=kps-1290]

nets (from the schematic view):
  N1: IC1.Enable_1, Uno.D3_PWM
  N2: IC1.In_1, Uno.D7
  N3: IC1.Out_1_(_Controlled_by_Enable_1_), M1.pin_2
  N4: IC1.0V, Uno.GND, Battery_Switch.O
  N5: IC1.Out_2_(_Controlled_by_Enable_1_), M1.pin_1
  N6: IC1.In_2, Uno.D8
  N7: IC1.+Vmotor, VCC2.+
  N8: IC1.Enable_2, Uno.D5_PWM
  N9: IC1.In_3, Uno.D12/MISO
  N10: IC1.Out_3_(_Controlled_by_Enable_2_), M2.pin_2
  N11: IC1.Out_4_(_Controlled_by_Enable_2_), M2.pin_1
  N12: IC1.In_4, Uno.D13/SCK
  N13: IC1.+V, 5V_power_switch.O
  N14: Uno.5V, 5V_power_switch.P
  N15: Uno.VIN, VCC3.+
  N16: VCC2.-, VCC3.-, Battery_Switch.P

notes:
  Frsky X8R Receiver
  red and black are power
  blue: ch1
  green: ch2
  yellow: ch3
